# Fritzing sketch fritzing_layout (saved by Fritzing 0.9.2b)
breadboards: 1

parts:
  R1 = Resistor [tolerance=±5% resistance=220 package=THT]
  Power_Supply = DC Power [voltage=5V]
  C1 = Electrolytic Capacitor [capacitance=1mF package="100 mil [THT, electrolytic]"]
  Arduino = Arduino Pro Mini v13
  LED_Strip = ws2812b [package="smd 2812b"]

nets:
  N1: R1.Pin_0, LED_Strip.DIN
  N2: R1.Pin_1, Arduino.D6_PWM
  VCC: Power_Supply.V+, C1.+, Arduino.VCC, LED_Strip.VDD
  GND: Power_Supply.V-, C1.-, Arduino.GND, LED_Strip.VSS

notes:
  WS8211B strip with 77 RGB LEDs
  arduino 5V
  C1 - Protect the LEDs from the first power surge
  R1 - Dampen reflections on the data line
  More LEDs daisy chained
